# Fritzing sketch qm-rpi-scan Proto Hat Wiring (saved by Fritzing 0.9.9b)

parts:
  Part2 = Adafruit Perma-Proto HAT [part_number="Adafruit #2314 and #2310"]
  Part3 = RFID-RC522-v2
  J2 = Piezo Speaker
  LED2 = smd LED [color="Red (633nm)" package="0805 [SMD]"]
  F2 = Small Fan, based on Fan - Ventilador [package=THT]
  J3 = Screw terminal - 2 pins [package=THT]
  J5 = Screw terminal - 2 pins [package=THT]
  R3 = Resistor [tolerance=±5% resistance=330 package=THT]

nets:
  N1: Part2.GPIO25, Part2.N$13#220
  N2: Part2.SPI_MOSI, Part2.N$9#200
  N3: Part2.SPI_MISO, Part2.N$10#205
  N4: Part2.SPI_SCLK, Part2.N$7#190
  N5: Part2.SPI_CE0, Part2.N$8#195
  N6: Part2.GPIO16, Part2.N$42#280
  N7: Part2.GPIO21, Part2.N$23#264
  N8: Part2.GND, Part2.N$12#212, Part2.N$45#292, Part2.N$61#375, J2.pin1
  N9: Part2.3.3V, Part2.N$14#225
  N10: Part2.5.0V, Part2.N$62#380
  N11: Part2.N$7#186, Part3.SCK
  N12: Part2.N$8#191, Part3.SDA
  N13: Part2.N$9#196, Part3.MOSI
  N14: Part2.N$10#201, Part3.MISO
  N15: Part2.N$12#211, Part3.GND
  N16: Part2.N$13#216, Part3.RST
  N17: Part2.N$14#221, Part3.3.3V
  N18: Part2.N$21#251, LED2.cathode, J3.pin1
  N19: Part2.N$21#254, R3.Pin_1
  N20: Part2.N$23#261, LED2.anode, J3.pin2
  N21: Part2.N$42#278, J2.pin2
  N22: Part2.N$45#295, R3.Pin_0
  N23: Part2.N$61#372, F2.GND, J5.pin2
  N24: Part2.N$62#377, F2.5V, J5.pin1

custom parts:
  Adafruit Perma-Proto HAT: To kick off the Adafruit HAT party, we have this Perma-Proto inspired plug in daughter board. It has a grid of 0.1" prototyping soldering holes for attaching chips, resistors, LED, potentiometers and more. The holes are connected underneath with traces to mimic the solderless breadboards you're familiar. There's also long power strips for +3V, +5V and Ground connections to the Pi. Near the top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
  RFID-RC522-v2: A simple China made RFID-RC522 Reader; do check the pin labels, as this is a MFRC522 based clone.
  Small Fan, based on Fan - Ventilador: Small 2-pin fan, commonly used with single-board computers, 3d-printers, etc. This work is based on a much larger fan, as commonly found in desktop computers
