# Fritzing sketch qm-rpi-scan Wiring (saved by Fritzing 0.9.9b)

parts:
  Part1 = RFID-RC522-v2
  LED1 = smd LED [color="Red (633nm)" package="0805 [SMD]"]
  R2 = Resistor [tolerance=±5% resistance=330 package=THT]
  J1 = Piezo Speaker
  Mod1 = Raspberry Pi 4B
  F1 = Small Fan, based on Fan - Ventilador [package=THT]

nets:
  N1: Part1.SDA, Mod1.GPIO8
  N2: Part1.SCK, Mod1.GPIO11
  N3: Part1.MOSI, Mod1.GPIO10
  N4: Part1.MISO, Mod1.GPIO9
  GND: Part1.GND, R2.Pin_1, J1.pin1, Mod1.GND, F1.GND
  N5: Part1.RST, Mod1.GPIO25
  3.3V: Part1.3.3V, Mod1.3V3
  N6: LED1.cathode, R2.Pin_0
  N7: LED1.anode, Mod1.GPIO21
  N8: J1.pin2, Mod1.GPIO16
  5V: Mod1.5V, F1.5V

custom parts:
  RFID-RC522-v2: A simple China made RFID-RC522 Reader; do check the pin labels, as this is a MFRC522 based clone.
  Small Fan, based on Fan - Ventilador: Small 2-pin fan, commonly used with single-board computers, 3d-printers, etc. This work is based on a much larger fan, as commonly found in desktop computers
